// Logisim project 4-bit Register.circ as structural Verilog: 1 circuit, main circuit main
module main (
  input  MSB,
  input  in_2,
  input  in_3,
  input  LSB,
  input  Write_Clock,
  output MSB_2,
  output out_7,
  output Q,
  output LSB_2,
  output out_10,
  output out_11,
  output Not_Q,
  output out_13
);

  wire nand_1_out, nand_2_out, nand_3_out, nand_4_out, nand_5_out, nand_6_out, nand_7_out, nand_8_out,
       nand_9_out, nand_10_out, nand_11_out, nand_12_out;

  nand nand_1 (nand_1_out, LSB, LSB);
  nand nand_2 (nand_2_out, MSB, MSB);
  nand nand_3 (nand_3_out, in_2, Write_Clock);
  nand nand_4 (nand_4_out, in_2, in_2);
  nand nand_5 (nand_5_out, in_3, Write_Clock);
  nand nand_6 (nand_6_out, in_3, in_3);
  nand nand_7 (nand_7_out, LSB, Write_Clock);
  nand nand_8 (nand_8_out, MSB, Write_Clock);
  nand nand_9 (nand_9_out, nand_2_out, Write_Clock);
  nand nand_10 (nand_10_out, nand_4_out, Write_Clock);
  nand nand_11 (nand_11_out, nand_6_out, Write_Clock);
  nand nand_12 (nand_12_out, nand_1_out, Write_Clock);
  nand nand_13 (LSB_2, nand_7_out, out_10);
  nand nand_14 (out_10, LSB_2, nand_12_out);
  nand nand_15 (MSB_2, nand_8_out, out_13);
  nand nand_16 (out_13, MSB_2, nand_9_out);
  nand nand_17 (out_7, nand_3_out, Not_Q);
  nand nand_18 (Not_Q, out_7, nand_10_out);
  nand nand_19 (Q, nand_5_out, out_11);
  nand nand_20 (out_11, Q, nand_11_out);
endmodule
