// Logisim project LFSR.circ as structural Verilog: 1 circuit, main circuit main
module main (
);

  wire clock_1_out, register_1_q, register_2_q, register_3_q, xor_1_out;

  Clock clock_1 (.out(clock_1_out));
  Register #(.width(1)) register_1 (.D(xor_1_out), .Q(register_1_q), .clk(clock_1_out));  // open: en, clr
  xor xor_1 (xor_1_out, register_3_q, register_2_q);
  Register #(.width(1)) register_2 (.D(register_1_q), .Q(register_2_q), .clk(clock_1_out));  // open: en, clr
  Register #(.width(1)) register_3 (.D(register_2_q), .Q(register_3_q), .clk(clock_1_out));  // open: en, clr

  // Notes on the sheet:
  //   Seed: 1 0 0
  //   C3 = 1
  //   C2 = 0
  //   C1 = 1
  //   C0 = 1
endmodule
