// Logisim project 3bit decoder.circ as structural Verilog: 1 circuit, main circuit main
module main (
  input  Select0,
  input  Select1,
  input  Select2,
  output Output_0,
  output Output1,
  output Output_2,
  output Output_3,
  output Output_4,
  output Output_5,
  output Output_6,
  output Output_7
);

  wire not_1_out, not_2_out, not_3_out;

  not not_1 (not_1_out, Select0);
  not not_2 (not_2_out, Select1);
  not not_3 (not_3_out, Select2);
  and and_1 (Output_0, not_1_out, not_2_out, not_3_out);
  and and_2 (Output1, Select0, not_2_out, not_3_out);
  and and_3 (Output_2, not_1_out, Select1, not_3_out);
  and and_4 (Output_3, Select0, Select1, not_3_out);
  and and_5 (Output_4, not_1_out, not_2_out, Select2, Select2);
  and and_6 (Output_5, not_2_out, Select0, Select2);
  and and_7 (Output_6, not_1_out, Select1, Select2);
  and and_8 (Output_7, Select0, Select1, Select2);
endmodule
