// Logisim project Mux.circ as structural Verilog: 1 circuit, main circuit main
module main (
  input  Select_0,
  input  Select_1,
  input  Select_2,
  input  input_0,
  input  input_1,
  input  input_2,
  input  input_3,
  input  input_4,
  input  input_5,
  input  input_6,
  input  input_7,
  output out_12
);

  wire and_1_out, and_2_out, and_3_out, and_4_out, and_5_out, and_6_out, and_7_out, and_8_out, and_9_out,
       and_10_out, and_11_out, and_12_out, and_13_out, and_14_out, and_15_out, and_16_out, not_1_out,
       not_2_out, not_3_out, or_1_out, or_2_out, or_3_out, or_4_out;

  not not_1 (not_1_out, Select_0);
  not not_2 (not_2_out, Select_1);
  not not_3 (not_3_out, Select_2);
  and and_1 (and_1_out, not_2_out, input_1);
  and and_2 (and_2_out, input_2, Select_1);
  and and_3 (and_3_out, Select_0, input_3);
  and and_4 (and_4_out, Select_2, input_4);
  and and_5 (and_5_out, Select_0, Select_2, input_5);
  and and_6 (and_6_out, Select_2, Select_1, input_6);
  and and_7 (and_7_out, Select_1, input_7, Select_0);
  and and_8 (and_8_out, not_1_out, not_3_out, input_0);
  and and_9 (and_9_out, and_8_out, not_2_out);
  and and_10 (and_10_out, Select_0, not_3_out, and_1_out);
  and and_11 (and_11_out, not_1_out, not_3_out, and_2_out);
  and and_12 (and_12_out, Select_1, not_3_out, and_3_out);
  and and_13 (and_13_out, not_1_out, not_2_out, and_4_out);
  and and_14 (and_14_out, not_2_out, and_5_out);
  and and_15 (and_15_out, not_1_out, and_6_out);
  and and_16 (and_16_out, Select_2, and_7_out);
  or or_1 (or_1_out, and_9_out, and_10_out);
  or or_2 (or_2_out, and_11_out, and_12_out);
  or or_3 (or_3_out, and_13_out, and_14_out);
  or or_4 (or_4_out, and_15_out, and_16_out);
  or or_5 (out_12, or_1_out, or_2_out, or_3_out, or_4_out);
endmodule
