// Logisim project 4-bit adder.circ as structural Verilog: 1 circuit, main circuit main
module main (
  input  MSB,
  input  in_2,
  input  in_3,
  input  LSB,
  input  MSB_2,
  input  in_6,
  input  in_7,
  input  LSB_2,
  input  Carry,
  output Overflow,
  output MSB_3,
  output out_12,
  output out_13,
  output LSB_3
);

  wire and_1_out, and_2_out, and_3_out, and_4_out, and_5_out, and_6_out, and_7_out, and_8_out, or_1_out,
       or_2_out, or_3_out, xor_1_out, xor_3_out, xor_4_out, xor_6_out;

  and and_1 (and_1_out, LSB, LSB_2);
  xor xor_1 (xor_1_out, LSB, LSB_2);
  and and_2 (and_2_out, xor_1_out, Carry);
  xor xor_2 (LSB_3, xor_1_out, Carry);
  or or_1 (or_1_out, and_2_out, and_1_out);
  xor xor_3 (xor_3_out, in_3, in_7);
  and and_3 (and_3_out, in_3, in_7);
  xor xor_4 (xor_4_out, in_2, in_6);
  and and_4 (and_4_out, in_2, in_6);
  and and_5 (and_5_out, xor_3_out, or_1_out);
  and and_6 (and_6_out, xor_4_out, or_2_out);
  xor xor_5 (out_13, xor_3_out, or_1_out);
  or or_2 (or_2_out, and_5_out, and_3_out);
  xor xor_6 (xor_6_out, MSB, MSB_2);
  and and_7 (and_7_out, MSB, MSB_2);
  xor xor_7 (out_12, xor_4_out, or_2_out);
  or or_3 (or_3_out, and_6_out, and_4_out);
  and and_8 (and_8_out, xor_6_out, or_3_out);
  xor xor_8 (MSB_3, xor_6_out, or_3_out);
  or or_4 (Overflow, and_8_out, and_7_out);

  // Notes on the sheet:
  //   1-bit adder
  //   carry
  //   1-bit adder
  //   1-bit adder
  //   carry
  //   carry
  //   1-bit adder
  //   carry
endmodule
