// Logisim project Simple 8bit Computer v3.circ as structural Verilog: 2 circuits, main circuit main
module main (
  input  Reset,
  input  Ground,
  output [7:0] AddressBus,
  output [7:0] RAMDataIn,
  output [7:0] RAMDataOut,
  output [7:0] A_Register,
  output [7:0] X_Register,
  output [7:0] Y_Register,
  output [7:0] PC_Register,
  output [7:0] Instruction,
  output [7:0] XYSum
);

  wire adder_1_cout, and_1_out, and_2_out, and_3_out, BusOffset_q, CarryBit_q, Clock_out, counter_1_q,
       decoder_1_out1, decoder_1_out2, decoder_1_out3, decoder_1_out4, decoder_1_out5, decoder_1_out7,
       decoder_1_out8, decoder_1_out9, decoder_1_out11, decoder_1_out12, IROffset_q, not_1_out, not_2_out,
       not_3_out, not_4_out, or_1_out, or_2_out, or_3_out, or_4_out, or_5_out, or_6_out;
  wire [3:0] bit_extender_1_out, OperandRegister_q, OperandRegister_q_2;
  wire [7:0] DataInBuffer_q, multiplexer_2_out, multiplexer_3_out, multiplexer_4_out, register_1_q;

  Counter #(.width(1), .max('h1)) counter_1 (
    .count(and_1_out), .Q(counter_1_q), .clk(and_1_out));  // open: load, D, carry, clr
  and and_1 (and_1_out, decoder_1_out12, and_2_out);
  or or_1 (or_1_out, decoder_1_out11, and_3_out);
  Multiplexer #(.width(8)) multiplexer_1 (
    .in0(PC_Register), .in1(register_1_q), .out(AddressBus), .sel(counter_1_q));  // open: en
  Register DataInBuffer (.D(RAMDataIn), .Q(DataInBuffer_q), .clk(Clock_out), .clr(not_1_out));  // open: en
  not not_1 (not_1_out, Ground);
  not not_2 (not_2_out, or_1_out);
  and and_2 (and_2_out, not_3_out, decoder_1_out12);
  Multiplexer #(.width(8)) multiplexer_2 (
    .in0(DataInBuffer_q), .in1(RAMDataIn), .out(multiplexer_2_out), .sel(counter_1_q));  // open: en
  or or_2 (or_2_out, counter_1_q, Ground);
  not not_3 (not_3_out, Clock_out);
  Counter u_PC_Register (
    .load(or_1_out), .D({OperandRegister_q, OperandRegister_q_2}), .count(not_2_out), .Q(PC_Register),
    .clk(Clock_out), .clr(Reset));  // open: carry
  and and_3 (and_3_out, decoder_1_out7, CarryBit_q);
  Register InstructionRegister (.D(RAMDataOut), .en(Clock_out), .Q(Instruction), .clk(IROffset_q), .clr(Reset));
  Counter #(.width(1), .max('h1)) IROffset (
    .count(Clock_out), .Q(IROffset_q), .clk(Clock_out), .clr(Reset));  // open: load, D, carry
  Bit_Extender #(.out_width(4), .\type ("input")) bit_extender_1 (
    .in(Instruction), .out(bit_extender_1_out));  // open: extend
  Decoder #(.select(4)) decoder_1 (
    .out1(decoder_1_out1), .out2(decoder_1_out2), .out3(decoder_1_out3), .out4(decoder_1_out4),
    .out5(decoder_1_out5), .out7(decoder_1_out7), .out8(decoder_1_out8), .out9(decoder_1_out9),
    .out11(decoder_1_out11), .out12(decoder_1_out12), .sel(bit_extender_1_out));  // open: out0, out6, out10, out13, out14, out15, en
  RAM #(.bus("separate")) ram_1 (
    .addr(AddressBus), .din(multiplexer_2_out), .data(RAMDataOut), .str(or_2_out), .clk(Clock_out));  // open: sel, ld, clr
  Multiplexer #(.width(8)) multiplexer_3 (
    .in0({OperandRegister_q, OperandRegister_q_2}), .in1(RAMDataOut), .out(multiplexer_3_out),
    .sel(decoder_1_out12));  // open: en
  Counter #(.width(1), .max('h1)) BusOffset (
    .count(Clock_out), .Q(BusOffset_q), .clk(Clock_out), .clr(Reset));  // open: load, D, carry
  not not_4 (not_4_out, BusOffset_q);
  or or_3 (or_3_out, Ground, decoder_1_out12);
  Register register_1 (.D(multiplexer_3_out), .en(and_2_out), .Q(register_1_q), .clk(and_2_out));  // open: clr
  Register OperandRegister (
    .D(RAMDataOut), .en(not_4_out), .Q({OperandRegister_q, OperandRegister_q_2}), .clk(not_4_out), .clr(Reset));
  or or_4 (or_4_out, or_3_out, counter_1_q);
  Multiplexer #(.width(8), .disabled(0)) multiplexer_4 (
    .in0({OperandRegister_q, OperandRegister_q_2}), .in1(XYSum), .out(multiplexer_4_out), .sel(decoder_1_out4));  // open: en
  or or_5 (or_5_out, decoder_1_out4, decoder_1_out3);
  Clock Clock (.out(Clock_out));
  CPU_Registers CPU_Registers (
    .DataBusIn(multiplexer_4_out), .ARegister(A_Register), .YRegister(Y_Register), .DataBusOut(RAMDataIn),
    .XRegister(X_Register), .ClockIn(Clock_out), .ClearAllRegisters(Reset), .XRegisterWrite(decoder_1_out1),
    .YRegisterWrite(decoder_1_out2), .ARegisterWrite(or_5_out), .RegisterRead0(or_4_out),
    .RegisterRead1(Ground), .AReg2XReg(decoder_1_out9));
  Hex_Digit_Display hex_digit_display_1 (.value(PC_Register[3:0]));  // open: dp
  Hex_Digit_Display hex_digit_display_2 (.value(PC_Register[7:4]));  // open: dp
  Hex_Digit_Display hex_digit_display_3 (.value(A_Register[7:4]));  // open: dp
  Hex_Digit_Display hex_digit_display_4 (.value(Y_Register[7:4]));  // open: dp
  Adder adder_1 (.a(X_Register), .b(Y_Register), .out(XYSum), .cin(adder_1_cout), .cout(adder_1_cout));
  Hex_Digit_Display hex_digit_display_5 (.value(A_Register[3:0]));  // open: dp
  Hex_Digit_Display hex_digit_display_6 (.value(Y_Register[3:0]));  // open: dp
  Hex_Digit_Display hex_digit_display_7 (.value(X_Register[7:4]));  // open: dp
  Hex_Digit_Display hex_digit_display_8 (.value(Instruction[7:4]));  // open: dp
  Counter #(.width(1), .max('h1)) CarryBit (
    .count(or_6_out), .Q(CarryBit_q), .clk(or_6_out), .clr(decoder_1_out8));  // open: load, D, carry
  or or_6 (or_6_out, adder_1_cout, decoder_1_out5);
  Hex_Digit_Display hex_digit_display_9 (.value(X_Register[3:0]));  // open: dp
  Hex_Digit_Display hex_digit_display_10 (.value(Instruction[3:0]));  // open: dp
  Hex_Digit_Display hex_digit_display_11 (.value(OperandRegister_q_2));  // open: dp
  Hex_Digit_Display hex_digit_display_12 (.value(OperandRegister_q));  // open: dp

  // Notes on the sheet:
  //   PC Register
  //   Y Register
  //   A Register
  //   Instruction Register
  //   X Register
  //   Operand Register
  //   08 CLC --> clear carry
  //   09 TAX --> Store A in X
  //   OPCodes:
  //   01: LDX -- >Store value in X
  //   02: LDY --> Store Value in Y
  //   03: LDA --> Store value in A
  //   04 ADC --> add X to Y store in A
  //   05 SEC --> Set/toggle carry
  //   07 BCS --> must set carry then jump
  //   to memory pos
  //   0b JMP --> jmp to memory pos
  //   0c STA --> store A to memory pos
endmodule

module CPU_Registers (
  input  ClearAllRegisters,
  input  ClockIn,
  input  XRegisterWrite,
  input  YRegisterWrite,
  input  ARegisterWrite,
  input  RegisterRead0,
  input  [7:0] DataBusIn,
  input  RegisterRead1,
  input  AReg2XReg,
  output [7:0] XRegister,
  output [7:0] DataBusOut,
  output [7:0] YRegister,
  output [7:0] ARegister
);

  wire or_1_out;
  wire [7:0] controlled_buffer_1_out, multiplexer_1_out;

  Multiplexer #(.width(8)) multiplexer_1 (
    .in0(DataBusIn), .in1(controlled_buffer_1_out), .out(multiplexer_1_out), .sel(AReg2XReg));  // open: en
  or or_1 (or_1_out, XRegisterWrite, AReg2XReg);
  Register X_Register (.D(multiplexer_1_out), .en(or_1_out), .Q(XRegister), .clk(ClockIn), .clr(ClearAllRegisters));
  Register Y_Register (.D(DataBusIn), .en(YRegisterWrite), .Q(YRegister), .clk(ClockIn), .clr(ClearAllRegisters));
  Register A_Register (.D(DataBusIn), .en(ARegisterWrite), .Q(ARegister), .clk(ClockIn), .clr(ClearAllRegisters));
  assign controlled_buffer_1_out = AReg2XReg ? ARegister : 8'bz;  // Controlled_Buffer controlled_buffer_1
  Multiplexer #(.select(2), .width(8), .enable("false")) multiplexer_2 (
    .in1(ARegister), .in2(XRegister), .in3(YRegister), .out(DataBusOut), .sel({RegisterRead1, RegisterRead0}));  // open: in0
endmodule
